# Fritzing sketch Curiosity_FINAL  (saved by Fritzing 0.9.2b)

parts:
  BATT1 = 4xAA Switchable Battery Pack w/Bare Wire
  Componente2 = Arduino Sensor Shield v5.0
  J4 = Basic Servo
  M1 = DC Motor
  M2 = DC Motor
  M3 = DC Motor
  M4 = DC Motor
  M5 = DC Motor
  M6 = DC Motor
  S1 = H-Bridge with L298N
  BT1 = Bluetooth HC-06u [package=THT]
  Parte1 = Arduino Mega 2560 (Rev3)
  J1 = Basic Servo
  J3 = Basic Servo
  J2 = Basic Servo

nets:
  VIN: BATT1.POS, S1.12V, Parte1.VIN
  GND: BATT1.NEG, S1.GND, Parte1.GND
  D10: Componente2.D10, S1.IN2
  D8: Componente2.D8, S1.IN4
  D9: Componente2.D9, S1.IN3
  N1: Componente2.D12, J1.pulse
  N2: Componente2.D2, J4.pulse
  D3: Componente2.D3, S1.IN1
  N3: Componente2.D4, J3.pulse
  N4: Componente2.D7, J2.pulse
  N5: Componente2.+5V#90, J3.vcc
  N6: Componente2.+5V#92, J4.vcc
  5V: Componente2.+5V#94, Componente2.+5V#104, Componente2.+5V#109, J1.vcc, J2.vcc
  GND_2: Componente2.GND#114, Componente2.GND#115, Componente2.GND#119, Componente2.GND#124, J1.gnd, J2.gnd
  N7: Componente2.GND#129, J4.gnd
  N8: Componente2.GND#144, J3.gnd
  N9: M1.pin_1, M2.pin_1, M3.pin_1, S1.M2-02
  N10: M1.pin_2, M2.pin_2, M3.pin_2, S1.M2-01
  N11: M4.pin_1, M5.pin_1, M6.pin_1, S1.M1-02
  N12: M4.pin_2, M5.pin_2, M6.pin_2, S1.M1-01
  N13: BT1.TXD, Parte1.D18/TX1
  N14: BT1.RXD, Parte1.D19/RX1

custom parts:
  4xAA Switchable Battery Pack w/Bare Wire: 4xAA Switchable Battery Pack with Bare Wire connection
  H-Bridge with L298N: h-bridge
  Bluetooth HC-06u: Bluetooth HC-06 - face up, pins down 16.5mm x 37.5mm PCB
